// Logisim project PRUEBA_OR_AND.circ as structural Verilog: 1 circuit, main circuit main
module main (
  input  in_1,
  input  in_2,
  input  in_3,
  input  in_4,
  input  in_5,
  input  in_6
);

  wire and_1_out, and_2_out, and_3_out, and_4_out, and_5_out, not_1_out, not_2_out, not_3_out, or_1_out;

  not not_1 (not_1_out, in_2);
  not not_2 (not_2_out, in_1);
  and and_1 (and_1_out, in_2, in_1);
  or or_1 (or_1_out, not_1_out, not_2_out);
  LED led_1 (.in(and_1_out));
  not not_3 (not_3_out, or_1_out);
  LED led_2 (.in(not_3_out));
  and and_2 (and_2_out, in_4, in_3, in_5, in_6);
  and and_3 (and_3_out, in_3, in_4);
  and and_4 (and_4_out, in_5, in_6);
  and and_5 (and_5_out, and_3_out, and_4_out);
  LED led_3 (.in(and_2_out));
  LED led_4 (.in(and_5_out));
endmodule
