// Logisim project RAMsito.circ as structural Verilog: 3 circuits, main circuit main
module main (
  input  in_1,
  input  in_2,
  input  in_3,
  input  in_4,
  input  in_5,
  input  in_6,
  input  in_7,
  input  in_8,
  input  in_9,
  input  DIRECCION,
  input  in_11,
  input  in_12,
  input  nWE,
  input  nCS,
  output out_15,
  output out_16,
  output out_17,
  output out_18,
  output out_19,
  output out_20,
  output out_21,
  output out_22
);

  wire memory_ram_1_s1, memory_ram_1_s2, memory_ram_1_s3, memory_ram_1_s4, memory_ram_2_s1, memory_ram_2_s2,
       memory_ram_2_s3, memory_ram_2_s4;

  memory_ram memory_ram_1 (
    .nWE(nWE), .nCS(nCS), .A0(in_12), .A1(in_11), .A2(DIRECCION), .A3(in_9), .D0(in_4), .D1(in_3), .D2(in_2),
    .D3(in_1), .S1(memory_ram_1_s1), .S2(memory_ram_1_s2), .S3(memory_ram_1_s3), .S4(memory_ram_1_s4));
  memory_ram memory_ram_2 (
    .nWE(nWE), .nCS(nCS), .A0(in_12), .A1(in_11), .A2(DIRECCION), .A3(in_9), .D0(in_8), .D1(in_7), .D2(in_6),
    .D3(in_5), .S1(memory_ram_2_s1), .S2(memory_ram_2_s2), .S3(memory_ram_2_s3), .S4(memory_ram_2_s4));
  IC7404 ic7404_1 (
    .D1(memory_ram_1_s1), .D2(memory_ram_1_s2), .D3(memory_ram_1_s3), .D4(memory_ram_1_s4), .S1(out_18),
    .S2(out_17), .S3(out_16), .S4(out_15));  // open: D5, D6, S5, S6
  IC7404 ic7404_2 (
    .D1(memory_ram_2_s1), .D2(memory_ram_2_s2), .D3(memory_ram_2_s3), .D4(memory_ram_2_s4), .S1(out_22),
    .S2(out_21), .S3(out_20), .S4(out_19));  // open: D5, D6, S5, S6
  Hex_Digit_Display #(.decimalPoint("false")) hex_digit_display_1 (.value({out_15, out_16, out_17, out_18}));
  Hex_Digit_Display #(.decimalPoint("false")) hex_digit_display_2 (.value({out_19, out_20, out_21, out_22}));

  // Notes on the sheet:
  //   DATOS DE ENTRADA
  //   SALIDA EN BINARIO
  //   HEXADECIMAL
endmodule

module memory_ram (
  input  nWE,
  input  nCS,
  input  A0,
  input  A1,
  input  A2,
  input  A3,
  input  D0,
  input  D1,
  input  D2,
  input  D3,
  output S1,
  output S2,
  output S3,
  output S4
);

  wire and_1_out, and_2_out, CLK_out, not_1_out, not_2_out, not_3_out, not_4_out;
  wire [3:0] ram_1_dout;

  not not_1 (not_1_out, nWE);
  not not_2 (not_2_out, nCS);
  and and_1 (and_1_out, not_1_out, not_2_out);
  Clock CLK (.out(CLK_out));
  not not_3 (not_3_out, not_1_out);
  not not_4 (not_4_out, nCS);
  RAM #(.addrWidth(4), .dataWidth(4)) ram_1 (
    .addr({A3, A2, A1, A0}), .we(and_1_out), .oe(and_2_out), .clk(CLK_out), .din({D3, D2, D1, D0}),
    .dout(ram_1_dout));
  and and_2 (and_2_out, not_3_out, not_4_out);
  assign S1 = and_2_out ? ~ram_1_dout[0] : 1'bz;  // Controlled_Inverter controlled_inverter_1
  assign S2 = and_2_out ? ~ram_1_dout[1] : 1'bz;  // Controlled_Inverter controlled_inverter_2
  assign S3 = and_2_out ? ~ram_1_dout[2] : 1'bz;  // Controlled_Inverter controlled_inverter_3
  assign S4 = and_2_out ? ~ram_1_dout[3] : 1'bz;  // Controlled_Inverter controlled_inverter_4
  Hex_Digit_Display #(.decimalPoint("false")) hex_digit_display_1 (.value({S4, S3, S2, S1}));
endmodule

module IC7404 (
  input  D1,
  input  D2,
  input  D3,
  input  D4,
  input  D5,
  input  D6,
  output S1,
  output S2,
  output S3,
  output S4,
  output S5,
  output S6
);

  not not_1 (S1, D1);
  not not_2 (S2, D2);
  not not_3 (S3, D3);
  not not_4 (S4, D4);
  not not_5 (S5, D5);
  not not_6 (S6, D6);
endmodule
